// Logisim project clock_assignment.circ as structural Verilog: 1 circuit, main circuit main
module main (
);

  wire A_out, and_1_out, button_1_out, clock_1_out, counter_1_carry, counter_3_carry;
  wire [3:0] counter_1_q, counter_3_q;

  Register register_1 ();  // open: D, en, clk, Q, clr
  Clock clock_1 (.out(clock_1_out));
  Counter #(.max('h9), .width(4)) counter_1 (
    .clr(button_1_out), .clk(clock_1_out), .carry(counter_1_carry), .Q(counter_1_q));  // open: load, up, count, D
  Hex_Digit_Display hex_digit_display_1 ();  // open: value, dp
  Counter counter_2 ();  // open: clr, load, up, count, clk, D, carry, Q
  DotMatrix dotmatrix_1 ();  // open: col0, col1, col2, col3, col4
  _7_Segment_Display u_7_segment_display_1 ();  // open: g, f, a, b, e, d, c, dp
  Hex_Digit_Display hex_digit_display_2 (.value(counter_3_q));  // open: dp
  Counter #(.max('h5), .width(4)) counter_3 (
    .clr(button_1_out), .count(counter_1_carry), .clk(clock_1_out), .carry(counter_3_carry), .Q(counter_3_q));  // open: load, up, D
  Hex_Digit_Display hex_digit_display_3 (.value(counter_1_q));  // open: dp
  Button button_1 (.out(button_1_out));
  and and_1 (and_1_out, counter_1_carry, counter_3_carry);
  Button A (.out(A_out));
  // OR_Gate or_1 has open pins: in0=and_1_out, in1=A_out, out=open
endmodule
