// Logisim project cpu_fetch_decode_execute.circ as structural Verilog: 1 circuit, main circuit main
module main (
  input  CLK_STEP,
  output T0_FETCH,
  output T1_DECODE,
  output T2_EXEC,
  output T3_STORE,
  output [3:0] OPCODE,
  output [7:0] ACC_VAL
);

  wire [1:0] PhaseCtr_q;
  wire [3:0] PC_p3;
  wire [7:0] adder_1_out, bit_extender_1_out, multiplexer_1_out, rom_1_data;
  wire [7:4] IR_q;

  // Counter #(.width(4), .max('hf)) PC: pin names not known; wires that end beside it: CLK_STEP, CLK_STEP, PC_p3
  Counter #(.width(2), .max('h3)) PhaseCtr (.Q(PhaseCtr_q));  // open: load, D, count, carry, clk, clr
  Decoder #(.select(2), .enable("false")) decoder_1 (
    .out0(CLK_STEP), .out1(T1_DECODE), .out2(T2_EXEC), .out3(T3_STORE), .sel(PhaseCtr_q));
  ROM #(.addrWidth(4), .dataWidth(8)) rom_1 (.addr(PC_p3), .data(rom_1_data));  // open: sel
  Register #(.width(8)) IR (.D(rom_1_data), .Q({IR_q, OPCODE}), .clk(CLK_STEP));  // open: en, clr
  assign bit_extender_1_out = {{4{1'b0}}, IR_q};  // Bit_Extender bit_extender_1
  Adder adder_1 (.a(bit_extender_1_out), .b(ACC_VAL), .out(adder_1_out));  // open: cin, cout
  Multiplexer #(.width(8), .enable("false")) multiplexer_1 (
    .in0(bit_extender_1_out), .out(multiplexer_1_out));  // open: in1, sel
  Register #(.width(8)) ACC (.D(multiplexer_1_out), .Q(ACC_VAL));  // open: en, clk, clr

  assign T0_FETCH = CLK_STEP;

  // Notes on the sheet:
  //   contents of rom_1 (hex, n*v repeats v):
  //   15 23 24
endmodule
