// Logisim project memory_basic.circ as structural Verilog: 1 circuit, main circuit main
// Input
module main (
  input  [7:0] Address,
  input  [7:0] Data
);

  wire clock_1_out;
  wire [7:0] register_1_q;

  Clock clock_1 (.out(clock_1_out));
  Register register_1 (.D(Address), .en(1'b1), .clk(clock_1_out), .Q(register_1_q));  // open: clr
  Register register_2 ();  // open: D, en, clk, Q, clr
  RAM ram_1 (.addr(register_1_q), .we(1'b1), .clk(clock_1_out), .din(Data));  // open: oe, dout
endmodule
