// Logisim project simple_cpu_v1a.circ as structural Verilog: 12 circuits, main circuit simple_cpu_v1a
module simple_cpu_v1a (
);

  wire clock_1_out, CLR_out, control_logic_1_acc_en, control_logic_1_addr_sel, control_logic_1_data_sel,
       control_logic_1_ir_en, control_logic_1_pc_en, control_logic_1_pc_ld, control_logic_1_ram_we,
       zero_1_out_2;
  wire [2:0] control_logic_1_alu_ctl0;
  wire [3:0] counter_8_1_q, counter_8_1_q_2, Memory_data_2, mux_2_8_2_z, mux_2_8_2_z_2;
  wire [7:0] alu_1_q, mux_2_8_1_z, reg_8_1_q;
  wire [11:0] Memory_data;
  wire [15:0] reg_16_1_out_5;

  Clock clock_1 (.out(clock_1_out));
  Button CLR (.out(CLR_out));
  Button CLK (.out(clock_1_out));
  Hex_Digit_Display hex_digit_display_1 (.value(Memory_data_2));  // open: dp
  Hex_Digit_Display hex_digit_display_2 (.value(Memory_data[11:8]));  // open: dp
  Hex_Digit_Display hex_digit_display_3 (.value(Memory_data[7:4]));  // open: dp
  Hex_Digit_Display hex_digit_display_4 (.value(Memory_data[3:0]));  // open: dp
  reg_16 reg_16_1 (
    .CLR(CLR_out), .EN(control_logic_1_ir_en), .CLK(clock_1_out), .D({Memory_data_2, Memory_data}),
    .out_5(reg_16_1_out_5));
  LED led_1 (.in(zero_1_out_2));
  Hex_Digit_Display hex_digit_display_5 (.value(reg_16_1_out_5[15:12]));  // open: dp
  Hex_Digit_Display hex_digit_display_6 (.value(reg_16_1_out_5[11:8]));  // open: dp
  zero zero_1 (.D(reg_8_1_q), .out_2(zero_1_out_2));
  Hex_Digit_Display hex_digit_display_7 (.value(reg_16_1_out_5[7:4]));  // open: dp
  Hex_Digit_Display hex_digit_display_8 (.value(reg_16_1_out_5[3:0]));  // open: dp
  Hex_Digit_Display hex_digit_display_9 (.value(counter_8_1_q_2));  // open: dp
  counter_8 counter_8_1 (
    .CLR(CLR_out), .EN(control_logic_1_pc_en), .CLK(clock_1_out), .LD(control_logic_1_pc_ld),
    .D(reg_16_1_out_5[7:0]), .Q({counter_8_1_q_2, counter_8_1_q}));
  control_logic control_logic_1 (
    .CLR(CLR_out), .CLK(clock_1_out), .A0(reg_16_1_out_5[12]), .A1(reg_16_1_out_5[13]),
    .A2(reg_16_1_out_5[14]), .A3(reg_16_1_out_5[15]), .Z(zero_1_out_2), .IR_EN(control_logic_1_ir_en),
    .ADDR_SEL(control_logic_1_addr_sel), .RAM_WE(control_logic_1_ram_we),
    .DATA_SEL(control_logic_1_data_sel), .PC_LD(control_logic_1_pc_ld), .PC_EN(control_logic_1_pc_en),
    .ACC_EN(control_logic_1_acc_en), .ALU_CTL2(control_logic_1_alu_ctl0[2]),
    .ALU_CTL1(control_logic_1_alu_ctl0[1]), .ALU_CTL0(control_logic_1_alu_ctl0[0]));  // open: ROM_EN, RAM_EN
  mux_2_8 mux_2_8_1 (.EN(control_logic_1_data_sel), .A(reg_16_1_out_5[7:0]), .B(Memory_data[7:0]), .Z(mux_2_8_1_z));
  Hex_Digit_Display hex_digit_display_10 (.value(counter_8_1_q));  // open: dp
  Hex_Digit_Display hex_digit_display_11 (.value(mux_2_8_2_z_2));  // open: dp
  mux_2_8 mux_2_8_2 (
    .EN(control_logic_1_addr_sel), .A({counter_8_1_q_2, counter_8_1_q}), .B(reg_16_1_out_5[7:0]),
    .Z({mux_2_8_2_z_2, mux_2_8_2_z}));
  alu alu_1 (.A(reg_8_1_q), .B(mux_2_8_1_z), .CTL(control_logic_1_alu_ctl0), .Q(alu_1_q));
  Hex_Digit_Display hex_digit_display_12 (.value(mux_2_8_2_z));  // open: dp
  Hex_Digit_Display hex_digit_display_13 (.value(4'b0000));  // open: dp
  Hex_Digit_Display hex_digit_display_14 (.value(reg_8_1_q[7:4]));  // open: dp
  reg_8 reg_8_1 (.CLR(CLR_out), .EN(control_logic_1_acc_en), .CLK(clock_1_out), .D(alu_1_q), .Q(reg_8_1_q));
  Hex_Digit_Display hex_digit_display_15 (.value(4'b0000));  // open: dp
  LED led_2 (.in(control_logic_1_ram_we));
  Hex_Digit_Display hex_digit_display_16 (.value(reg_8_1_q[3:0]));  // open: dp
  Hex_Digit_Display hex_digit_display_17 (.value(reg_8_1_q[7:4]));  // open: dp
  Hex_Digit_Display hex_digit_display_18 (.value(reg_8_1_q[3:0]));  // open: dp
  RAM #(.dataWidth(16)) Memory (
    .addr({mux_2_8_2_z_2, mux_2_8_2_z}), .data({Memory_data_2, Memory_data}), .clk(control_logic_1_ram_we),
    .ld(1'b1));  // open: sel, clr

  // Notes on the sheet:
  //   DATA IN BUS
  //   IR
  //   ZERO FLAG
  //   INSTRUCTION REG
  //   PC
  //   DATA MUX
  //   PROGRAM COUNTER
  //   ADDR BUS
  //   ADDR MUX
  //   ACCUMULATOR
  //   ACC
  //   DATA OUT BUS
  //   WRITE
  //   MEMORY
endmodule

module control_logic (
  input  CLR,
  input  CLK,
  input  A0,
  input  A1,
  input  A2,
  input  A3,
  input  Z,
  output IR_EN,
  output ROM_EN,
  output RAM_EN,
  output ADDR_SEL,
  output RAM_WE,
  output DATA_SEL,
  output PC_LD,
  output PC_EN,
  output ACC_EN,
  output ALU_CTL2,
  output ALU_CTL1,
  output ALU_CTL0
);

  wire and_1_out, and_2_out, and_6_out, and_7_out, not_1_out, not_2_out, onehot_decoder_16_1_y0,
       onehot_decoder_16_1_y1, onehot_decoder_16_1_y2, onehot_decoder_16_1_y3, onehot_decoder_16_1_y4,
       onehot_decoder_16_1_y5, onehot_decoder_16_1_y6, onehot_decoder_16_1_y7, onehot_decoder_16_1_y8,
       onehot_decoder_16_1_y9, onehot_decoder_16_1_ya, or_1_out, or_2_out, or_4_out, or_7_out,
       ring_counter_3_1_q0, ring_counter_3_1_q1, ring_counter_3_1_q2;

  ring_counter_3 ring_counter_3_1 (
    .RST(CLR), .CLK(CLK), .Q0(ring_counter_3_1_q0), .Q1(ring_counter_3_1_q1), .Q2(ring_counter_3_1_q2));
  onehot_decoder_16 onehot_decoder_16_1 (
    .A0(A0), .A1(A1), .A2(A2), .A3(A3), .Y0(onehot_decoder_16_1_y0), .Y1(onehot_decoder_16_1_y1),
    .Y2(onehot_decoder_16_1_y2), .Y3(onehot_decoder_16_1_y3), .Y4(onehot_decoder_16_1_y4),
    .Y5(onehot_decoder_16_1_y5), .Y6(onehot_decoder_16_1_y6), .Y7(onehot_decoder_16_1_y7),
    .Y8(onehot_decoder_16_1_y8), .Y9(onehot_decoder_16_1_y9), .YA(onehot_decoder_16_1_ya));  // open: YB, YC, YD, YE, YF
  not not_1 (not_1_out, Z);
  buf buffer_1 (IR_EN, ring_counter_3_1_q0);
  buf buffer_2 (ROM_EN, ring_counter_3_1_q0);
  or or_1 (or_1_out, ring_counter_3_1_q1, ring_counter_3_1_q2);
  or or_2 (or_2_out, onehot_decoder_16_1_y4, onehot_decoder_16_1_y5, onehot_decoder_16_1_y6, onehot_decoder_16_1_y7);
  or or_3 (DATA_SEL, onehot_decoder_16_1_y4, onehot_decoder_16_1_y6, onehot_decoder_16_1_y7);
  and and_1 (and_1_out, Z, onehot_decoder_16_1_y9);
  and and_2 (and_2_out, onehot_decoder_16_1_ya, not_1_out);
  or or_4 (or_4_out, onehot_decoder_16_1_y0, onehot_decoder_16_1_y1, onehot_decoder_16_1_y2, onehot_decoder_16_1_y3, onehot_decoder_16_1_y4, onehot_decoder_16_1_y6, onehot_decoder_16_1_y7);
  or or_5 (ALU_CTL2, onehot_decoder_16_1_y0, onehot_decoder_16_1_y4);
  buf buffer_3 (ALU_CTL1, onehot_decoder_16_1_y3);
  or or_6 (ALU_CTL0, onehot_decoder_16_1_y7, onehot_decoder_16_1_y2);
  and and_3 (RAM_EN, or_1_out, or_2_out);
  and and_4 (RAM_WE, ring_counter_3_1_q2, onehot_decoder_16_1_y5);
  or or_7 (or_7_out, onehot_decoder_16_1_y8, and_1_out, and_2_out);
  buf buffer_4 (ADDR_SEL, RAM_EN);
  and and_5 (ACC_EN, ring_counter_3_1_q2, or_4_out);
  not not_2 (not_2_out, or_7_out);
  and and_6 (and_6_out, not_2_out, ring_counter_3_1_q1);
  and and_7 (and_7_out, or_7_out, ring_counter_3_1_q2);
  buf buffer_5 (PC_LD, or_7_out);
  or or_8 (PC_EN, and_6_out, and_7_out);
endmodule

module reg_16 (
  input  CLR,
  input  EN,
  input  CLK,
  input  [15:0] D,
  output [15:0] out_5
);

  reg_8 reg_8_1 (.CLR(CLR), .EN(EN), .CLK(CLK), .D(D[7:0]), .Q(out_5[7:0]));
  reg_8 reg_8_2 (.CLR(CLR), .EN(EN), .CLK(CLK), .D(D[15:8]), .Q(out_5[15:8]));
endmodule

module counter_8 (
  input  CLR,
  input  EN,
  input  CLK,
  input  LD,
  input  [7:0] D,
  output [7:0] Q
);

  wire not_1_out;
  wire [7:0] adder_1_out, mux_2_8_1_z;

  mux_2_8 mux_2_8_1 (.EN(LD), .A(Q), .B(D), .Z(mux_2_8_1_z));
  not not_1 (not_1_out, LD);
  Adder adder_1 (.a(mux_2_8_1_z), .b({8{1'b0}}), .out(adder_1_out), .cin(not_1_out));  // open: cout
  reg_8 reg_8_1 (.CLR(CLR), .EN(EN), .CLK(CLK), .D(adder_1_out), .Q(Q));
endmodule

module zero (
  input  [7:0] D,
  output out_2
);

  nor nor_1 (out_2, D[0], D[1], D[2], D[3], D[4], D[5], D[6], D[7]);
endmodule

module mux_2_8 (
  input  EN,
  input  [7:0] A,
  input  [7:0] B,
  output [7:0] Z
);

  Multiplexer #(.enable("true")) multiplexer_1 (.in0(A[0]), .in1(B[0]), .out(Z[0]), .sel(EN), .en(1'b1));
  Multiplexer #(.enable("true")) multiplexer_2 (.in0(A[1]), .in1(B[1]), .out(Z[1]), .sel(EN), .en(1'b1));
  Multiplexer #(.enable("true")) multiplexer_3 (.in0(A[2]), .in1(B[2]), .out(Z[2]), .sel(EN), .en(1'b1));
  Multiplexer #(.enable("true")) multiplexer_4 (.in0(A[3]), .in1(B[3]), .out(Z[3]), .sel(EN), .en(1'b1));
  Multiplexer #(.enable("true")) multiplexer_5 (.in0(A[4]), .in1(B[4]), .out(Z[4]), .sel(EN), .en(1'b1));
  Multiplexer #(.enable("true")) multiplexer_6 (.in0(A[5]), .in1(B[5]), .out(Z[5]), .sel(EN), .en(1'b1));
  Multiplexer #(.enable("true")) multiplexer_7 (.in0(A[6]), .in1(B[6]), .out(Z[6]), .sel(EN), .en(1'b1));
  Multiplexer #(.enable("true")) multiplexer_8 (.in0(A[7]), .in1(B[7]), .out(Z[7]), .sel(EN), .en(1'b1));
endmodule

module alu (
  input  [7:0] A,
  input  [7:0] B,
  input  [2:0] CTL,
  output [7:0] Q
);

  wire [7:0] adder_1_out, and_2_8_1_z, mux_2_8_1_z, mux_2_8_2_z, subtractor_1_out;

  Adder adder_1 (.a(A), .b(B), .out(adder_1_out));  // open: cin, cout
  Subtractor subtractor_1 (.a(A), .b(B), .out(subtractor_1_out));  // open: bin, bout
  and_2_8 and_2_8_1 (.A(A), .B(B), .Z(and_2_8_1_z));
  mux_2_8 mux_2_8_1 (.EN(CTL[0]), .A(adder_1_out), .B(subtractor_1_out), .Z(mux_2_8_1_z));
  mux_2_8 mux_2_8_2 (.EN(CTL[1]), .A(mux_2_8_1_z), .B(and_2_8_1_z), .Z(mux_2_8_2_z));
  mux_2_8 mux_2_8_3 (.EN(CTL[2]), .A(mux_2_8_2_z), .B(B), .Z(Q));
endmodule

module reg_8 (
  input  CLR,
  input  EN,
  input  CLK,
  input  [7:0] D,
  output [7:0] Q
);

  reg_4 reg_4_1 (
    .CLR(CLR), .EN(EN), .CLK(CLK), .D0(D[0]), .D1(D[1]), .D2(D[2]), .D3(D[3]), .Q0(Q[0]), .Q1(Q[1]),
    .Q2(Q[2]), .Q3(Q[3]));
  reg_4 reg_4_2 (
    .CLR(CLR), .EN(EN), .CLK(CLK), .D0(D[4]), .D1(D[5]), .D2(D[6]), .D3(D[7]), .Q0(Q[4]), .Q1(Q[5]),
    .Q2(Q[6]), .Q3(Q[7]));
endmodule

module reg_4 (
  input  CLR,
  input  EN,
  input  CLK,
  input  D0,
  input  D1,
  input  D2,
  input  D3,
  output Q0,
  output Q1,
  output Q2,
  output Q3
);

  D_Flip_Flop d_ff_1 (.clk(CLR), .preset(Q0));  // open: D, Q, Qn, reset
  D_Flip_Flop d_ff_2 (.clk(CLR), .preset(Q1));  // open: D, Q, Qn, reset
  D_Flip_Flop d_ff_3 (.clk(CLR), .preset(Q2));  // open: D, Q, Qn, reset
  D_Flip_Flop d_ff_4 (.clk(CLR), .preset(Q3));  // open: D, Q, Qn, reset
endmodule

module and_2_8 (
  input  [7:0] A,
  input  [7:0] B,
  output [7:0] Z
);

  and and_1 (Z[0], A[0], B[0]);
  and and_2 (Z[1], A[1], B[1]);
  and and_3 (Z[2], A[2], B[2]);
  and and_4 (Z[3], A[3], B[3]);
  and and_5 (Z[4], A[4], B[4]);
  and and_6 (Z[5], A[5], B[5]);
  and and_7 (Z[6], A[6], B[6]);
  and and_8 (Z[7], A[7], B[7]);
endmodule

module onehot_decoder_16 (
  input  A0,
  input  A1,
  input  A2,
  input  A3,
  output Y0,
  output Y1,
  output Y2,
  output Y3,
  output Y4,
  output Y5,
  output Y6,
  output Y7,
  output Y8,
  output Y9,
  output YA,
  output YB,
  output YC,
  output YD,
  output YE,
  output YF
);

  wire not_1_out, not_2_out, not_3_out, not_4_out;

  not not_1 (not_1_out, A0);
  not not_2 (not_2_out, A1);
  not not_3 (not_3_out, A2);
  not not_4 (not_4_out, A3);
  and and_1 (Y0, not_1_out, not_2_out, not_3_out, not_4_out);
  and and_2 (Y1, A0, not_2_out, not_3_out, not_4_out);
  and and_3 (Y2, not_1_out, A1, not_3_out, not_4_out);
  and and_4 (Y3, A0, A1, not_3_out, not_4_out);
  and and_5 (Y4, not_1_out, not_2_out, A2, not_4_out);
  and and_6 (Y5, A0, not_2_out, A2, not_4_out);
  and and_7 (Y6, not_1_out, A1, A2, not_4_out);
  and and_8 (Y7, A0, A1, A2, not_4_out);
  and and_9 (Y8, not_1_out, not_2_out, not_3_out, A3);
  and and_10 (Y9, A0, not_2_out, not_3_out, A3);
  and and_11 (YA, not_1_out, A1, not_3_out, A3);
  and and_12 (YB, A0, A1, not_3_out, A3);
  and and_13 (YC, not_1_out, not_2_out, A2, A3);
  and and_14 (YD, A0, A1, not_3_out, A3);
  and and_15 (YE, not_1_out, A1, A2, A3);
  and and_16 (YF, A0, A1, A2, A3);
endmodule

module ring_counter_3 (
  input  RST,
  input  CLK,
  output Q0,
  output Q1,
  output Q2
);

  D_Flip_Flop d_ff_1 (.clk(1'b0), .preset(Q0), .reset(1'b1));  // open: D, Q, Qn
  D_Flip_Flop d_ff_2 (.clk(RST), .preset(Q1), .reset(1'b1));  // open: D, Q, Qn
  D_Flip_Flop d_ff_3 (.clk(CLK), .D(Q1), .Q(Q2), .preset(1'b0), .reset(RST));  // open: Qn
endmodule
